# Fritzing sketch HSS_node_2send (saved by Fritzing 0.9.2b)
circuit board: 8.46667cm x 5.64444cm
breadboards: 1

parts:
  PIR1 = PIR sensor
  NRF24L2 = NRF24L01
  Part2 = Arduino Pro Mini v13
  3V_Converter = LD33 Low-Dropout Voltage Regulator
  5V_converter = Voltage Regulator - 5V [package="TO220 [THT]"]
  VCC1 = Battery
  NOR_gate = SN74LS20N [package="DIP14 [THT]"]

nets:
  N1: PIR1.VDD, 5V_converter.output_voltage
  N2: PIR1.SIG, NOR_gate.1D
  GND: PIR1.GND, NRF24L2.GND, Part2.GND, 3V_Converter.GND, 5V_converter.GND, VCC1.-, NOR_gate.1Y, NOR_gate.GND, NOR_gate.2A
  VCC: NRF24L2.VCC, Part2.RAW, 3V_Converter.Vout, NOR_gate.VCC
  N3: NRF24L2.CSN, Part2.D10_PWM/SS
  N4: NRF24L2.MOSI, Part2.D11_PWM/MOSI
  N5: NRF24L2.IRQ, Part2.D2
  N6: NRF24L2.CE, Part2.D9_PWM
  N7: NRF24L2.SCK, Part2.D13/SCK
  N8: NRF24L2.MISO, Part2.D12/MISO
  N9: Part2.D3_PWM, NOR_gate.1C
  N10: 3V_Converter.Vin, 5V_converter.input_voltage, VCC1.+

custom parts:
  NRF24L01: NRF24L01 module
