# Fritzing sketch HSS_node_4send_v0_1 (saved by Fritzing 0.9.2b)
circuit board: 8.46667cm x 5.64444cm
breadboards: 1

parts:
  U1 = SN74LS20N [package="DIP14 [THT]"]
  U2 = SM130 [package=sm130]
  Part1 = Arduino Uno (Rev3)

nets:
  N1: U1.1C, Part1.D3_PWM
  N2: U1.1D, U2.ANT2, Part1.D4
  GND: U1.1Y, U1.GND, U2.GND, Part1.GND
  VCC: U1.VCC, Part1.3V3
  VCC_2: U2.VCC, Part1.5V
